// Logisim project CPU_8_Bit_PAGING - Copy.circ as structural Verilog: 20 circuits, main circuit main
module main (
  input  Manual_Input,
  input  [7:0] in_2,
  input  [3:0] in_3,
  input  [3:0] in_4,
  input  Reg_Clr,
  input  RSET,
  output [3:0] out_7
);

  wire clock_1_out, clock_2_out, control_unit_1_counter_load, control_unit_1_load_read_enbl,
       control_unit_1_store_write_enbl, controlled_buffer_8_out, controlled_buffer_9_out,
       controlled_buffer_10_out, n7_segment_display_1_p1, n7_segment_display_2_p1, not_1_out;
  wire [1:0] control_unit_1_op_code;
  wire [3:0] control_unit_1_address, control_unit_1_counter_address, control_unit_1_page_select,
       controlled_buffer_3_out, controlled_buffer_4_out;
  wire [7:0] alu_1_alu_out, control_unit_1_a_input, control_unit_1_b_input, control_unit_1_main_bus_out,
       controlled_buffer_1_out, controlled_buffer_2_out, controlled_buffer_6_out,
       paging_registers_1_out_data_1, paging_registers_1_out_data_2;

  ALU alu_1 (
    .OP_CODE(control_unit_1_op_code), .A_INPUT(control_unit_1_a_input), .B_INPUT(control_unit_1_b_input),
    .ALU_OUT(alu_1_alu_out));
  assign controlled_buffer_1_out = control_unit_1_store_write_enbl ? control_unit_1_main_bus_out : 8'bz;  // Controlled_Buffer controlled_buffer_1
  Control_Unit control_unit_1 (
    .INST_DATA(controlled_buffer_6_out), .MAIN_BUS_IN(controlled_buffer_1_out), .CLEAR(Reg_Clr),
    .ALU_OUTPUT(alu_1_alu_out), .ADDRESS(control_unit_1_address),
    .LOAD_READ_ENBL(control_unit_1_load_read_enbl), .STORE_WRITE_ENBL(control_unit_1_store_write_enbl),
    .MAIN_BUS_OUT(control_unit_1_main_bus_out), .Counter_Address(control_unit_1_counter_address),
    .Page_Select(control_unit_1_page_select), .Counter_Load(control_unit_1_counter_load),
    .A_INPUT(control_unit_1_a_input), .B_INPUT(control_unit_1_b_input), .OP_CODE(control_unit_1_op_code));
  assign controlled_buffer_2_out = Manual_Input ? in_2 : 8'bz;  // Controlled_Buffer controlled_buffer_2
  assign controlled_buffer_3_out = Manual_Input ? in_3 : 4'bz;  // Controlled_Buffer controlled_buffer_3
  assign controlled_buffer_4_out = Manual_Input ? in_4 : 4'bz;  // Controlled_Buffer controlled_buffer_4
  assign controlled_buffer_2_out = not_1_out ? controlled_buffer_1_out : 8'bz;  // Controlled_Buffer controlled_buffer_5
  assign controlled_buffer_6_out = not_1_out ? paging_registers_1_out_data_2 : 8'bz;  // Controlled_Buffer controlled_buffer_6
  Clock clock_1 (.out(clock_1_out));
  not not_1 (not_1_out, Manual_Input);
  assign controlled_buffer_3_out = not_1_out ? control_unit_1_address : 4'bz;  // Controlled_Buffer controlled_buffer_7
  assign controlled_buffer_8_out = not_1_out ? control_unit_1_store_write_enbl : 1'bz;  // Controlled_Buffer controlled_buffer_8
  assign controlled_buffer_9_out = not_1_out ? control_unit_1_load_read_enbl : 1'bz;  // Controlled_Buffer controlled_buffer_9
  assign controlled_buffer_10_out = not_1_out ? clock_1_out : 1'bz;  // Controlled_Buffer controlled_buffer_10
  assign controlled_buffer_1_out = controlled_buffer_9_out ? paging_registers_1_out_data_1 : 8'bz;  // Controlled_Buffer controlled_buffer_11
  assign controlled_buffer_8_out = Manual_Input ? Manual_Input : 1'bz;  // Controlled_Buffer controlled_buffer_12
  Clock clock_2 (.out(clock_2_out));
  Counter #(.max('hf), .trigger("falling"), .width(4)) counter_1 (
    .clr(RSET), .load(control_unit_1_counter_load), .up(not_1_out), .count(not_1_out),
    .clk(controlled_buffer_10_out), .D(control_unit_1_counter_address), .Q(out_7));  // open: carry
  assign controlled_buffer_4_out = not_1_out ? control_unit_1_page_select : 4'bz;  // Controlled_Buffer controlled_buffer_13
  Paging_Registers paging_registers_1 (
    .OUT_ADDR_1(controlled_buffer_3_out), .OUT_ADDR_2(out_7), .PAGE_SELECT(controlled_buffer_4_out),
    .REG_ADDR(controlled_buffer_3_out), .DATA_IN(controlled_buffer_2_out), .ENBL(controlled_buffer_8_out),
    .CLK(clock_2_out), .OUT_DATA_1(paging_registers_1_out_data_1), .OUT_DATA_2(paging_registers_1_out_data_2));
  // BCD_to_7_Segment_decoder bcd_to_7_segment_decoder_1: pin names not known
  // BCD_to_7_Segment_decoder bcd_to_7_segment_decoder_2: pin names not known
  // _7_Segment_Display 7_segment_display_1: pin names not known; wires that end beside it: n7_segment_display_1_p1, n7_segment_display_1_p1
  // _7_Segment_Display 7_segment_display_2: pin names not known; wires that end beside it: n7_segment_display_2_p1, n7_segment_display_2_p1
  // Binary_to_BCD_converter #(.binvalue(4)) binary_to_bcd_converter_1: pin names not known; wires that end beside it: out_7
endmodule

module Adder_8bit (
  input  in_1,
  input  in_2,
  input  in_3,
  input  in_4,
  input  in_5,
  input  in_6,
  input  in_7,
  input  in_8,
  input  in_9,
  input  in_10,
  input  in_11,
  input  in_12,
  input  in_13,
  input  in_14,
  input  in_15,
  input  in_16,
  output out_17,
  output out_18,
  output out_19,
  output out_20,
  output out_21,
  output out_22,
  output out_23,
  output out_24,
  output out_25
);

  wire full_adder_2_carry, full_adder_3_carry, full_adder_4_carry, full_adder_5_carry, full_adder_6_carry,
       full_adder_7_carry, full_adder_8_carry;

  Full_Adder full_adder_1 (.CIN(full_adder_2_carry), .A(in_1), .B(in_9), .CARRY(out_17), .SUM(out_18));
  Full_Adder full_adder_2 (.CIN(full_adder_3_carry), .A(in_2), .B(in_10), .CARRY(full_adder_2_carry), .SUM(out_19));
  Full_Adder full_adder_3 (.CIN(full_adder_4_carry), .A(in_3), .B(in_11), .CARRY(full_adder_3_carry), .SUM(out_20));
  Full_Adder full_adder_4 (.CIN(full_adder_5_carry), .A(in_4), .B(in_12), .CARRY(full_adder_4_carry), .SUM(out_21));
  Full_Adder full_adder_5 (.CIN(full_adder_6_carry), .A(in_5), .B(in_13), .CARRY(full_adder_5_carry), .SUM(out_22));
  Full_Adder full_adder_6 (.CIN(full_adder_7_carry), .A(in_6), .B(in_14), .CARRY(full_adder_6_carry), .SUM(out_23));
  Full_Adder full_adder_7 (.CIN(full_adder_8_carry), .A(in_7), .B(in_15), .CARRY(full_adder_7_carry), .SUM(out_24));
  Full_Adder full_adder_8 (.CIN(1'b0), .A(in_8), .B(in_16), .CARRY(full_adder_8_carry), .SUM(out_25));
endmodule

module Full_Adder (
  input  CIN,
  input  A,
  input  B,
  output CARRY,
  output SUM
);

  wire and_1_out, and_2_out, xor_1_out;

  and and_1 (and_1_out, A, B);
  and and_2 (and_2_out, CIN, xor_1_out);
  or or_1 (CARRY, and_1_out, and_2_out);
  xor xor_1 (xor_1_out, A, B);
  xor xor_2 (SUM, CIN, xor_1_out);
endmodule

module Subtractor_8bit (
  input  in_1,
  input  in_2,
  input  in_3,
  input  in_4,
  input  in_5,
  input  in_6,
  input  in_7,
  input  in_8,
  input  in_9,
  input  in_10,
  input  in_11,
  input  in_12,
  input  in_13,
  input  in_14,
  input  in_15,
  input  in_16,
  output out_17,
  output out_18,
  output out_19,
  output out_20,
  output out_21,
  output out_22,
  output out_23,
  output out_24,
  output out_25
);

  wire full_subtractor_2_out_4, full_subtractor_3_out_4, full_subtractor_4_out_4, full_subtractor_5_out_4,
       full_subtractor_6_out_4, full_subtractor_7_out_4, full_subtractor_8_out_4;

  Full_Subtractor full_subtractor_1 (.B(in_1), .A(in_9), .Cin(full_subtractor_2_out_4), .out_4(out_17), .SUB(out_18));
  Full_Subtractor full_subtractor_2 (
    .B(in_2), .A(in_10), .Cin(full_subtractor_3_out_4), .out_4(full_subtractor_2_out_4), .SUB(out_19));
  Full_Subtractor full_subtractor_3 (
    .B(in_3), .A(in_11), .Cin(full_subtractor_4_out_4), .out_4(full_subtractor_3_out_4), .SUB(out_20));
  Full_Subtractor full_subtractor_4 (
    .B(in_4), .A(in_12), .Cin(full_subtractor_5_out_4), .out_4(full_subtractor_4_out_4), .SUB(out_21));
  Full_Subtractor full_subtractor_5 (
    .B(in_5), .A(in_13), .Cin(full_subtractor_6_out_4), .out_4(full_subtractor_5_out_4), .SUB(out_22));
  Full_Subtractor full_subtractor_6 (
    .B(in_6), .A(in_14), .Cin(full_subtractor_7_out_4), .out_4(full_subtractor_6_out_4), .SUB(out_23));
  Full_Subtractor full_subtractor_7 (
    .B(in_7), .A(in_15), .Cin(full_subtractor_8_out_4), .out_4(full_subtractor_7_out_4), .SUB(out_24));
  Full_Subtractor full_subtractor_8 (.B(in_8), .A(in_16), .Cin(1'b0), .out_4(full_subtractor_8_out_4), .SUB(out_25));
endmodule

module Full_Subtractor (
  input  B,
  input  A,
  input  Cin,
  output out_4,
  output SUB
);

  wire and_1_out, and_2_out, not_1_out, not_2_out, xor_1_out;

  not not_1 (not_1_out, B);
  xor xor_1 (xor_1_out, B, A);
  and and_1 (and_1_out, A, not_1_out);
  not not_2 (not_2_out, xor_1_out);
  and and_2 (and_2_out, Cin, not_2_out);
  or or_1 (out_4, and_1_out, and_2_out);
  xor xor_2 (SUB, xor_1_out, Cin);
endmodule

module Incrementer (
  input  in_1,
  input  in_2,
  input  in_3,
  input  in_4,
  input  in_5,
  input  in_6,
  input  in_7,
  input  in_8,
  output out_9,
  output out_10,
  output out_11,
  output out_12,
  output out_13,
  output out_14,
  output out_15,
  output out_16,
  output out_17
);

  wire half_adder_2_carry, half_adder_3_carry, half_adder_4_carry, half_adder_5_carry, half_adder_6_carry,
       half_adder_7_carry, half_adder_8_carry;

  Half_Adder half_adder_1 (.A(in_1), .B(half_adder_2_carry), .CARRY(out_9), .SUM(out_10));
  Half_Adder half_adder_2 (.A(in_2), .B(half_adder_3_carry), .CARRY(half_adder_2_carry), .SUM(out_11));
  Half_Adder half_adder_3 (.A(in_3), .B(half_adder_4_carry), .CARRY(half_adder_3_carry), .SUM(out_12));
  Half_Adder half_adder_4 (.A(in_4), .B(half_adder_5_carry), .CARRY(half_adder_4_carry), .SUM(out_13));
  Half_Adder half_adder_5 (.A(in_5), .B(half_adder_6_carry), .CARRY(half_adder_5_carry), .SUM(out_14));
  Half_Adder half_adder_6 (.A(in_6), .B(half_adder_7_carry), .CARRY(half_adder_6_carry), .SUM(out_15));
  Half_Adder half_adder_7 (.A(in_7), .B(half_adder_8_carry), .CARRY(half_adder_7_carry), .SUM(out_16));
  Half_Adder half_adder_8 (.A(in_8), .B(1'b1), .CARRY(half_adder_8_carry), .SUM(out_17));
endmodule

module Half_Adder (
  input  A,
  input  B,
  output CARRY,
  output SUM
);

  and and_1 (CARRY, B, A);
  xor xor_1 (SUM, A, B);
endmodule

module Half_Subtractor (
  input  A,
  input  B,
  output BORROW,
  output DIFF
);

  wire not_1_out;

  not not_1 (not_1_out, A);
  and and_1 (BORROW, B, not_1_out);
  xor xor_1 (DIFF, A, B);
endmodule

module Decrementer (
  input  in_1,
  input  in_2,
  input  in_3,
  input  in_4,
  input  in_5,
  input  in_6,
  input  in_7,
  input  in_8,
  output out_9,
  output out_10,
  output out_11,
  output out_12,
  output out_13,
  output out_14,
  output out_15,
  output out_16,
  output out_17
);

  wire half_subtractor_2_borrow, half_subtractor_3_borrow, half_subtractor_4_borrow,
       half_subtractor_5_borrow, half_subtractor_6_borrow, half_subtractor_7_borrow, half_subtractor_8_borrow;

  Half_Subtractor half_subtractor_1 (.A(in_1), .B(half_subtractor_2_borrow), .BORROW(out_9), .DIFF(out_10));
  Half_Subtractor half_subtractor_2 (
    .A(in_2), .B(half_subtractor_3_borrow), .BORROW(half_subtractor_2_borrow), .DIFF(out_11));
  Half_Subtractor half_subtractor_3 (
    .A(in_3), .B(half_subtractor_4_borrow), .BORROW(half_subtractor_3_borrow), .DIFF(out_12));
  Half_Subtractor half_subtractor_4 (
    .A(in_4), .B(half_subtractor_5_borrow), .BORROW(half_subtractor_4_borrow), .DIFF(out_13));
  Half_Subtractor half_subtractor_5 (
    .A(in_5), .B(half_subtractor_6_borrow), .BORROW(half_subtractor_5_borrow), .DIFF(out_14));
  Half_Subtractor half_subtractor_6 (
    .A(in_6), .B(half_subtractor_7_borrow), .BORROW(half_subtractor_6_borrow), .DIFF(out_15));
  Half_Subtractor half_subtractor_7 (
    .A(in_7), .B(half_subtractor_8_borrow), .BORROW(half_subtractor_7_borrow), .DIFF(out_16));
  Half_Subtractor half_subtractor_8 (.A(in_8), .B(1'b1), .BORROW(half_subtractor_8_borrow), .DIFF(out_17));
endmodule

// 1
module ALU (
  input  [7:0] A_INPUT,
  input  [7:0] B_INPUT,
  input  [1:0] OP_CODE,
  output [7:0] ALU_OUT
);

  wire ADDER_out_17, ADDER_out_18, ADDER_out_19, ADDER_out_20, ADDER_out_21, ADDER_out_22, ADDER_out_23,
       ADDER_out_24, ADDER_out_25, and_1_out, and_2_out, and_3_out, and_4_out, and_5_out, and_6_out,
       and_7_out, and_8_out, and_9_out, and_10_out, and_11_out, and_12_out, and_13_out, and_14_out,
       and_15_out, and_16_out, and_17_out, and_18_out, and_19_out, and_20_out, and_21_out, and_22_out,
       and_23_out, and_24_out, and_25_out, and_26_out, and_27_out, and_28_out, and_29_out, and_30_out,
       and_31_out, and_32_out, decoder_1_out0, decoder_1_out1, decoder_1_out2, decoder_1_out3, DIVIDER_out_9,
       DIVIDER_out_11, DIVIDER_out_12, DIVIDER_out_13, DIVIDER_out_15, DIVIDER_out_16, DIVIDER_quotient,
       DIVIDER_remainder, MULTIPLYER_out_9, MULTIPLYER_out_10, MULTIPLYER_out_11, MULTIPLYER_out_12,
       MULTIPLYER_out_13, MULTIPLYER_out_14, MULTIPLYER_out_15, MULTIPLYER_out_16, SUBTRACTOR_out_17,
       SUBTRACTOR_out_18, SUBTRACTOR_out_19, SUBTRACTOR_out_20, SUBTRACTOR_out_21, SUBTRACTOR_out_22,
       SUBTRACTOR_out_23, SUBTRACTOR_out_24, SUBTRACTOR_out_25;

  and and_1 (and_1_out, decoder_1_out0, ADDER_out_18);
  Adder_8bit ADDER (
    .in_4(A_INPUT[4]), .in_5(A_INPUT[3]), .in_6(A_INPUT[2]), .in_7(A_INPUT[1]), .in_8(A_INPUT[0]),
    .in_1(A_INPUT[7]), .in_9(B_INPUT[7]), .in_10(B_INPUT[6]), .in_11(B_INPUT[5]), .in_12(B_INPUT[4]),
    .in_13(B_INPUT[3]), .in_14(B_INPUT[2]), .in_15(B_INPUT[1]), .in_16(B_INPUT[0]), .in_2(A_INPUT[6]),
    .in_3(A_INPUT[5]), .out_17(ADDER_out_17), .out_18(ADDER_out_18), .out_19(ADDER_out_19),
    .out_20(ADDER_out_20), .out_21(ADDER_out_21), .out_22(ADDER_out_22), .out_23(ADDER_out_23),
    .out_24(ADDER_out_24), .out_25(ADDER_out_25));
  and and_2 (and_2_out, decoder_1_out0, ADDER_out_19);
  and and_3 (and_3_out, decoder_1_out0, ADDER_out_20);
  and and_4 (and_4_out, decoder_1_out0, ADDER_out_21);
  and and_5 (and_5_out, ADDER_out_22, decoder_1_out0);
  and and_6 (and_6_out, ADDER_out_25, decoder_1_out0);
  and and_7 (and_7_out, ADDER_out_24, decoder_1_out0);
  and and_8 (and_8_out, ADDER_out_23, decoder_1_out0);
  Subtractor_8bit SUBTRACTOR (
    .in_4(A_INPUT[4]), .in_5(A_INPUT[3]), .in_6(A_INPUT[2]), .in_7(A_INPUT[1]), .in_8(A_INPUT[0]),
    .in_1(A_INPUT[7]), .in_9(B_INPUT[7]), .in_10(B_INPUT[6]), .in_11(B_INPUT[5]), .in_12(B_INPUT[4]),
    .in_13(B_INPUT[3]), .in_14(B_INPUT[2]), .in_15(B_INPUT[1]), .in_16(B_INPUT[0]), .in_2(A_INPUT[6]),
    .in_3(A_INPUT[5]), .out_17(SUBTRACTOR_out_17), .out_18(SUBTRACTOR_out_18), .out_19(SUBTRACTOR_out_19),
    .out_20(SUBTRACTOR_out_20), .out_21(SUBTRACTOR_out_21), .out_22(SUBTRACTOR_out_22),
    .out_23(SUBTRACTOR_out_23), .out_24(SUBTRACTOR_out_24), .out_25(SUBTRACTOR_out_25));
  and and_9 (and_9_out, decoder_1_out1, SUBTRACTOR_out_18);
  and and_10 (and_10_out, decoder_1_out1, SUBTRACTOR_out_19);
  and and_11 (and_11_out, decoder_1_out1, SUBTRACTOR_out_20);
  and and_12 (and_12_out, SUBTRACTOR_out_24, decoder_1_out1);
  and and_13 (and_13_out, SUBTRACTOR_out_23, decoder_1_out1);
  and and_14 (and_14_out, decoder_1_out1, SUBTRACTOR_out_21);
  and and_15 (and_15_out, SUBTRACTOR_out_22, decoder_1_out1);
  and and_16 (and_16_out, SUBTRACTOR_out_25, decoder_1_out1);
  and and_17 (and_17_out, decoder_1_out2, MULTIPLYER_out_9);
  and and_18 (and_18_out, decoder_1_out2, MULTIPLYER_out_10);
  and and_19 (and_19_out, decoder_1_out2, MULTIPLYER_out_11);
  Multiplier_4bit MULTIPLYER (
    .in_2(A_INPUT[2]), .in_3(A_INPUT[1]), .in_4(A_INPUT[0]), .in_5(B_INPUT[3]), .in_6(B_INPUT[2]),
    .in_7(B_INPUT[1]), .in_8(B_INPUT[0]), .in_1(A_INPUT[3]), .out_9(MULTIPLYER_out_9),
    .out_10(MULTIPLYER_out_10), .out_11(MULTIPLYER_out_11), .out_12(MULTIPLYER_out_12),
    .out_13(MULTIPLYER_out_13), .out_14(MULTIPLYER_out_14), .out_15(MULTIPLYER_out_15),
    .out_16(MULTIPLYER_out_16));
  and and_20 (and_20_out, MULTIPLYER_out_16, decoder_1_out2);
  and and_21 (and_21_out, MULTIPLYER_out_15, decoder_1_out2);
  and and_22 (and_22_out, MULTIPLYER_out_14, decoder_1_out2);
  and and_23 (and_23_out, decoder_1_out2, MULTIPLYER_out_12);
  and and_24 (and_24_out, MULTIPLYER_out_13, decoder_1_out2);
  and and_25 (and_25_out, decoder_1_out3, DIVIDER_out_9);
  and and_26 (and_26_out, decoder_1_out3, DIVIDER_quotient);
  Divider_4bit DIVIDER (
    .in_2(A_INPUT[2]), .in_3(A_INPUT[1]), .in_4(A_INPUT[0]), .in_5(B_INPUT[3]), .in_6(B_INPUT[2]),
    .in_7(B_INPUT[1]), .in_8(B_INPUT[0]), .in_1(A_INPUT[3]), .out_12(DIVIDER_out_12),
    .out_13(DIVIDER_out_13), .REMAINDER(DIVIDER_remainder), .out_15(DIVIDER_out_15), .out_16(DIVIDER_out_16),
    .out_9(DIVIDER_out_9), .QUOTIENT(DIVIDER_quotient), .out_11(DIVIDER_out_11));
  and and_27 (and_27_out, DIVIDER_out_15, decoder_1_out3);
  and and_28 (and_28_out, decoder_1_out3, DIVIDER_out_11);
  and and_29 (and_29_out, DIVIDER_remainder, decoder_1_out3);
  and and_30 (and_30_out, decoder_1_out3, DIVIDER_out_12);
  and and_31 (and_31_out, DIVIDER_out_13, decoder_1_out3);
  or or_1 (ALU_OUT[7], and_1_out, and_9_out, and_17_out, and_25_out);
  and and_32 (and_32_out, DIVIDER_out_16, decoder_1_out3);
  or or_2 (ALU_OUT[6], and_2_out, and_10_out, and_18_out, and_26_out);
  or or_3 (ALU_OUT[5], and_3_out, and_11_out, and_19_out, and_28_out);
  Decoder #(.select(2)) decoder_1 (
    .out0(decoder_1_out0), .out1(decoder_1_out1), .out2(decoder_1_out2), .out3(decoder_1_out3), .sel(OP_CODE));  // open: en
  or or_4 (ALU_OUT[4], and_4_out, and_14_out, and_23_out, and_30_out);
  or or_5 (ALU_OUT[3], and_5_out, and_15_out, and_24_out, and_31_out);
  or or_6 (ALU_OUT[2], and_8_out, and_13_out, and_22_out, and_29_out);
  or or_7 (ALU_OUT[1], and_7_out, and_12_out, and_21_out, and_27_out);
  or or_8 (ALU_OUT[0], and_6_out, and_16_out, and_20_out, and_32_out);

  // Notes on the sheet:
  //   ADDER
  //   SUBTRACTOR
  //   MULTIPLYER
  //   DIVIDER
endmodule

module Multiplier_4bit (
  input  in_1,
  input  in_2,
  input  in_3,
  input  in_4,
  input  in_5,
  input  in_6,
  input  in_7,
  input  in_8,
  output out_9,
  output out_10,
  output out_11,
  output out_12,
  output out_13,
  output out_14,
  output out_15,
  output out_16
);

  wire and_1_out, and_2_out, and_3_out, and_4_out, and_5_out, and_6_out, and_7_out, and_8_out, and_9_out,
       and_10_out, and_11_out, and_12_out, and_13_out, and_14_out, and_15_out, full_adder_2_carry,
       full_adder_2_sum, full_adder_3_carry, full_adder_4_carry, full_adder_4_sum, full_adder_5_carry,
       full_adder_6_carry, full_adder_6_sum, full_adder_7_carry, full_adder_7_sum, full_adder_8_carry,
       full_adder_8_sum, half_adder_1_carry, half_adder_1_sum, half_adder_2_carry, half_adder_3_carry,
       half_adder_4_carry;

  and and_1 (and_1_out, in_1, in_5);
  Full_Adder full_adder_1 (
    .CIN(full_adder_3_carry), .A(and_1_out), .B(full_adder_2_carry), .CARRY(out_9), .SUM(out_10));
  and and_2 (and_2_out, in_1, in_6);
  Full_Adder full_adder_2 (
    .CIN(full_adder_4_carry), .A(and_2_out), .B(half_adder_1_carry), .CARRY(full_adder_2_carry),
    .SUM(full_adder_2_sum));
  and and_3 (and_3_out, in_2, in_5);
  Full_Adder full_adder_3 (
    .CIN(full_adder_5_carry), .A(and_3_out), .B(full_adder_2_sum), .CARRY(full_adder_3_carry), .SUM(out_11));
  and and_4 (and_4_out, in_7, in_1);
  Half_Adder half_adder_1 (.A(and_4_out), .B(full_adder_6_carry), .CARRY(half_adder_1_carry), .SUM(half_adder_1_sum));
  and and_5 (and_5_out, in_2, in_6);
  Full_Adder full_adder_4 (
    .CIN(full_adder_7_carry), .A(half_adder_1_sum), .B(and_5_out), .CARRY(full_adder_4_carry),
    .SUM(full_adder_4_sum));
  and and_6 (and_6_out, in_3, in_5);
  Full_Adder full_adder_5 (
    .CIN(half_adder_2_carry), .A(and_6_out), .B(full_adder_4_sum), .CARRY(full_adder_5_carry), .SUM(out_12));
  and and_7 (and_7_out, in_1, in_8);
  and and_8 (and_8_out, in_7, in_2);
  Full_Adder full_adder_6 (
    .CIN(full_adder_8_carry), .A(and_8_out), .B(and_7_out), .CARRY(full_adder_6_carry), .SUM(full_adder_6_sum));
  and and_9 (and_9_out, in_3, in_6);
  Full_Adder full_adder_7 (
    .CIN(half_adder_3_carry), .A(full_adder_6_sum), .B(and_9_out), .CARRY(full_adder_7_carry),
    .SUM(full_adder_7_sum));
  and and_10 (and_10_out, in_4, in_5);
  Half_Adder half_adder_2 (.A(full_adder_7_sum), .B(and_10_out), .CARRY(half_adder_2_carry), .SUM(out_13));
  and and_11 (and_11_out, in_2, in_8);
  and and_12 (and_12_out, in_7, in_3);
  Full_Adder full_adder_8 (
    .CIN(half_adder_4_carry), .A(and_12_out), .B(and_11_out), .CARRY(full_adder_8_carry),
    .SUM(full_adder_8_sum));
  and and_13 (and_13_out, in_4, in_6);
  Half_Adder half_adder_3 (.A(full_adder_8_sum), .B(and_13_out), .CARRY(half_adder_3_carry), .SUM(out_14));
  and and_14 (and_14_out, in_3, in_8);
  and and_15 (and_15_out, in_7, in_4);
  Half_Adder half_adder_4 (.A(and_15_out), .B(and_14_out), .CARRY(half_adder_4_carry), .SUM(out_15));
  and and_16 (out_16, in_4, in_8);
endmodule

module Divider_4bit (
  input  in_1,
  input  in_2,
  input  in_3,
  input  in_4,
  input  in_5,
  input  in_6,
  input  in_7,
  input  in_8,
  output out_9,
  output QUOTIENT,
  output out_11,
  output out_12,
  output out_13,
  output REMAINDER,
  output out_15,
  output out_16
);

  wire divider_cell_1_d, divider_cell_1_not_b_202866c9, divider_cell_2_a_174802cb, divider_cell_2_co,
       divider_cell_2_not_b_202866c9, divider_cell_3_d, divider_cell_3_not_b_202866c9,
       divider_cell_4_a_174802cb, divider_cell_4_co, divider_cell_4_not_b_202866c9, divider_cell_5_d,
       divider_cell_5_not_b_202866c9, divider_cell_6_a_174802cb, divider_cell_6_co,
       divider_cell_6_not_b_202866c9, divider_cell_7_d, divider_cell_8_co, divider_cell_9_a_174802cb,
       divider_cell_9_co, divider_cell_9_not_b_202866c9, divider_cell_10_a_174802cb, divider_cell_10_co,
       divider_cell_10_not_b_202866c9, divider_cell_11_a_174802cb, divider_cell_11_co,
       divider_cell_11_not_b_202866c9, divider_cell_12_co, divider_cell_13_a_174802cb, divider_cell_13_co,
       divider_cell_13_not_b_202866c9, divider_cell_14_a_174802cb, divider_cell_14_co,
       divider_cell_14_not_b_202866c9, divider_cell_15_a_174802cb, divider_cell_15_co,
       divider_cell_15_not_b_202866c9, divider_cell_16_co, not_5_out, not_6_out, not_7_out, not_8_out;

  not not_1 (out_9, divider_cell_1_d);
  not not_2 (out_12, divider_cell_7_d);
  not not_3 (QUOTIENT, divider_cell_3_d);
  not not_4 (out_11, divider_cell_5_d);
  Divider_Cell divider_cell_1 (
    .N(divider_cell_1_d), .A(1'b0), .B(not_5_out), .CIN(divider_cell_2_co), .D(divider_cell_1_d),
    .NOT_B_202866c9(divider_cell_1_not_b_202866c9));  // open: CO, A_174802cb
  Divider_Cell divider_cell_2 (
    .N(divider_cell_1_d), .A(1'b0), .B(not_6_out), .CIN(divider_cell_9_co), .CO(divider_cell_2_co),
    .A_174802cb(divider_cell_2_a_174802cb), .NOT_B_202866c9(divider_cell_2_not_b_202866c9));  // open: D
  Divider_Cell divider_cell_3 (
    .N(divider_cell_3_d), .A(divider_cell_2_a_174802cb), .B(divider_cell_1_not_b_202866c9),
    .CIN(divider_cell_4_co), .D(divider_cell_3_d), .NOT_B_202866c9(divider_cell_3_not_b_202866c9));  // open: CO, A_174802cb
  Divider_Cell divider_cell_4 (
    .N(divider_cell_3_d), .A(divider_cell_9_a_174802cb), .B(divider_cell_2_not_b_202866c9),
    .CIN(divider_cell_10_co), .CO(divider_cell_4_co), .A_174802cb(divider_cell_4_a_174802cb),
    .NOT_B_202866c9(divider_cell_4_not_b_202866c9));  // open: D
  Divider_Cell divider_cell_5 (
    .N(divider_cell_5_d), .A(divider_cell_4_a_174802cb), .B(divider_cell_3_not_b_202866c9),
    .CIN(divider_cell_6_co), .D(divider_cell_5_d), .NOT_B_202866c9(divider_cell_5_not_b_202866c9));  // open: CO, A_174802cb
  Divider_Cell divider_cell_6 (
    .N(divider_cell_5_d), .A(divider_cell_10_a_174802cb), .B(divider_cell_4_not_b_202866c9),
    .CIN(divider_cell_11_co), .CO(divider_cell_6_co), .A_174802cb(divider_cell_6_a_174802cb),
    .NOT_B_202866c9(divider_cell_6_not_b_202866c9));  // open: D
  Divider_Cell divider_cell_7 (
    .N(divider_cell_7_d), .A(divider_cell_6_a_174802cb), .B(divider_cell_5_not_b_202866c9),
    .CIN(divider_cell_8_co), .D(divider_cell_7_d), .A_174802cb(out_13));  // open: CO, NOT_B_202866c9
  Divider_Cell divider_cell_8 (
    .N(divider_cell_7_d), .A(divider_cell_11_a_174802cb), .B(divider_cell_6_not_b_202866c9),
    .CIN(divider_cell_12_co), .CO(divider_cell_8_co), .A_174802cb(REMAINDER));  // open: D, NOT_B_202866c9
  Divider_Cell divider_cell_9 (
    .N(divider_cell_1_d), .A(1'b0), .B(not_7_out), .CIN(divider_cell_13_co), .CO(divider_cell_9_co),
    .A_174802cb(divider_cell_9_a_174802cb), .NOT_B_202866c9(divider_cell_9_not_b_202866c9));  // open: D
  Divider_Cell divider_cell_10 (
    .N(divider_cell_3_d), .A(divider_cell_13_a_174802cb), .B(divider_cell_9_not_b_202866c9),
    .CIN(divider_cell_14_co), .CO(divider_cell_10_co), .A_174802cb(divider_cell_10_a_174802cb),
    .NOT_B_202866c9(divider_cell_10_not_b_202866c9));  // open: D
  Divider_Cell divider_cell_11 (
    .N(divider_cell_5_d), .A(divider_cell_14_a_174802cb), .B(divider_cell_10_not_b_202866c9),
    .CIN(divider_cell_15_co), .CO(divider_cell_11_co), .A_174802cb(divider_cell_11_a_174802cb),
    .NOT_B_202866c9(divider_cell_11_not_b_202866c9));  // open: D
  Divider_Cell divider_cell_12 (
    .N(divider_cell_7_d), .A(divider_cell_15_a_174802cb), .B(divider_cell_11_not_b_202866c9),
    .CIN(divider_cell_16_co), .CO(divider_cell_12_co), .A_174802cb(out_15));  // open: D, NOT_B_202866c9
  not not_5 (not_5_out, in_5);
  not not_6 (not_6_out, in_6);
  not not_7 (not_7_out, in_7);
  Divider_Cell divider_cell_13 (
    .N(divider_cell_1_d), .A(in_1), .B(not_8_out), .CIN(1'b1), .CO(divider_cell_13_co),
    .A_174802cb(divider_cell_13_a_174802cb), .NOT_B_202866c9(divider_cell_13_not_b_202866c9));  // open: D
  Divider_Cell divider_cell_14 (
    .N(divider_cell_3_d), .A(in_2), .B(divider_cell_13_not_b_202866c9), .CIN(1'b1), .CO(divider_cell_14_co),
    .A_174802cb(divider_cell_14_a_174802cb), .NOT_B_202866c9(divider_cell_14_not_b_202866c9));  // open: D
  Divider_Cell divider_cell_15 (
    .N(divider_cell_5_d), .A(in_3), .B(divider_cell_14_not_b_202866c9), .CIN(1'b1), .CO(divider_cell_15_co),
    .A_174802cb(divider_cell_15_a_174802cb), .NOT_B_202866c9(divider_cell_15_not_b_202866c9));  // open: D
  Divider_Cell divider_cell_16 (
    .N(divider_cell_7_d), .A(in_4), .B(divider_cell_15_not_b_202866c9), .CIN(1'b1), .CO(divider_cell_16_co),
    .A_174802cb(out_16));  // open: D, NOT_B_202866c9
  not not_8 (not_8_out, in_8);
endmodule

module Modified_Full_Adder (
  input  CIN,
  input  A,
  input  B,
  output COUT,
  output OUT
);

  wire and_1_out, and_2_out, and_3_out, xor_1_out;

  and and_1 (and_1_out, A, B);
  and and_2 (and_2_out, A, CIN);
  and and_3 (and_3_out, B, CIN);
  xor xor_1 (xor_1_out, A, B);
  or or_1 (COUT, and_1_out, and_2_out, and_3_out);
  xor xor_2 (OUT, CIN, xor_1_out);
endmodule

module Divider_Cell (
  input  A,
  input  B,
  input  CIN,
  input  N,
  output CO,
  output D,
  output A_174802cb,
  output NOT_B_202866c9
);

  Modified_Full_Adder modified_full_adder_1 (.CIN(CIN), .A(A), .B(B), .COUT(CO), .OUT(D));
  Multiplexer multiplexer_1 (.in0(D), .in1(A), .out(A_174802cb), .sel(N));

  assign NOT_B_202866c9 = B;
endmodule

module Gated_Latch (
  input  DATA,
  input  WRITE_ENABLE_84b16714,
  output out_3
);

  wire and_1_out, and_2_out, not_1_out, not_2_out, or_1_out;

  and and_1 (and_1_out, DATA, WRITE_ENABLE_84b16714);
  not not_1 (not_1_out, DATA);
  and and_2 (and_2_out, not_1_out, WRITE_ENABLE_84b16714);
  or or_1 (or_1_out, out_3, and_1_out);
  not not_2 (not_2_out, and_2_out);
  and and_3 (out_3, or_1_out, not_2_out);
endmodule

module Main_Memory (
  input  [1:0] in_1,
  input  [1:0] in_2,
  input  in_3,
  input  in_4,
  input  in_5,
  input  D_in_out,
  input  Write_Enable,
  input  Read_Enable,
  input  in_9,
  input  in_10,
  input  in_11,
  input  in_12,
  input  in_13,
  input  in_14,
  input  in_15,
  input  in_16,
  input  in_17,
  input  in_18,
  input  [7:0] in_19,
  input  in_20,
  input  in_21,
  input  in_22,
  input  in_23,
  input  in_24,
  input  in_25,
  input  in_26,
  output out_27,
  output [7:0] out_28
);

  wire and_1_out, and_2_out, and_3_out, and_4_out, and_5_out, and_6_out, and_7_out, and_8_out, and_9_out,
       and_10_out, and_11_out, and_12_out, and_13_out, and_14_out, and_15_out, and_16_out, and_17_out,
       and_18_out, and_19_out, and_20_out, and_21_out, and_22_out, and_23_out, and_24_out, and_25_out,
       and_26_out, and_27_out, and_28_out, and_29_out, and_30_out, and_31_out, and_32_out, and_33_out,
       and_34_out, and_35_out, and_36_out, and_37_out, and_38_out, and_39_out, and_40_out, and_41_out,
       and_42_out, and_43_out, and_44_out, and_45_out, and_46_out, and_47_out, and_48_out,
       controlled_buffer_2_out, decoder_1_out0, decoder_1_out1, decoder_1_out2, decoder_1_out3,
       decoder_2_out0, decoder_2_out1, decoder_2_out2, decoder_2_out3, gated_latch_1_out_3,
       gated_latch_2_out_3, gated_latch_3_out_3, gated_latch_4_out_3, gated_latch_5_out_3,
       gated_latch_6_out_3, gated_latch_7_out_3, gated_latch_8_out_3, gated_latch_9_out_3,
       gated_latch_10_out_3, gated_latch_11_out_3, gated_latch_12_out_3, gated_latch_13_out_3,
       gated_latch_14_out_3, gated_latch_15_out_3, gated_latch_16_out_3, not_1_out, register_1_q,
       register_2_q, transistor_1_out;
  wire [7:0] register_3_q, undriven;

  not not_1 (not_1_out, in_4);
  Transistor transistor_1 (.in(in_3), .out(transistor_1_out), .gate(not_1_out));
  // Probe on transistor_1_out
  Controlled_Buffer controlled_buffer_1 (.out(out_27), .en(in_5));  // open: in
  Register #(.width(1)) register_1 (
    .D(controlled_buffer_2_out), .en(in_11), .clk(in_14), .Q(register_1_q), .clr(in_16));
  Decoder #(.select(2)) decoder_1 (
    .out0(decoder_1_out0), .out1(decoder_1_out1), .out2(decoder_1_out2), .out3(decoder_1_out3), .sel(in_2));  // open: en
  assign controlled_buffer_2_out = in_9 ? register_1_q : 1'bz;  // Controlled_Buffer controlled_buffer_2
  Decoder #(.select(2)) decoder_2 (
    .out0(decoder_2_out0), .out1(decoder_2_out1), .out2(decoder_2_out2), .out3(decoder_2_out3), .sel(in_1));  // open: en
  // Probe on controlled_buffer_2_out
  assign controlled_buffer_2_out = in_10 ? register_2_q : 1'bz;  // Controlled_Buffer controlled_buffer_3
  Register #(.width(1)) register_2 (
    .D(controlled_buffer_2_out), .en(in_12), .clk(in_15), .Q(register_2_q), .clr(in_17));
  and and_1 (and_1_out, decoder_1_out0, decoder_2_out0);
  and and_2 (and_2_out, decoder_1_out1, decoder_2_out0);
  and and_3 (and_3_out, decoder_1_out2, decoder_2_out0);
  and and_4 (and_4_out, decoder_1_out3, decoder_2_out0);
  and and_5 (and_5_out, and_1_out, Write_Enable);
  and and_6 (and_6_out, and_1_out, Read_Enable);
  and and_7 (and_7_out, and_2_out, Write_Enable);
  and and_8 (and_8_out, and_2_out, Read_Enable);
  and and_9 (and_9_out, and_3_out, Write_Enable);
  and and_10 (and_10_out, and_3_out, Read_Enable);
  and and_11 (and_11_out, and_4_out, Write_Enable);
  and and_12 (and_12_out, and_4_out, Read_Enable);
  assign out_28 = in_20 ? in_19 : 8'bz;  // Controlled_Buffer controlled_buffer_4
  assign D_in_out = and_6_out ? gated_latch_1_out_3 : 1'bz;  // Controlled_Buffer controlled_buffer_5
  Gated_Latch gated_latch_1 (.DATA(D_in_out), .WRITE_ENABLE_84b16714(and_5_out), .out_3(gated_latch_1_out_3));
  assign D_in_out = and_8_out ? gated_latch_2_out_3 : 1'bz;  // Controlled_Buffer controlled_buffer_6
  Gated_Latch gated_latch_2 (.DATA(D_in_out), .WRITE_ENABLE_84b16714(and_7_out), .out_3(gated_latch_2_out_3));
  assign D_in_out = and_10_out ? gated_latch_3_out_3 : 1'bz;  // Controlled_Buffer controlled_buffer_7
  Gated_Latch gated_latch_3 (.DATA(D_in_out), .WRITE_ENABLE_84b16714(and_9_out), .out_3(gated_latch_3_out_3));
  assign D_in_out = and_12_out ? gated_latch_4_out_3 : 1'bz;  // Controlled_Buffer controlled_buffer_8
  Gated_Latch gated_latch_4 (.DATA(D_in_out), .WRITE_ENABLE_84b16714(and_11_out), .out_3(gated_latch_4_out_3));
  Register register_3 (.D(out_28), .en(in_21), .clk(in_22), .Q(register_3_q), .clr(in_23));
  assign out_28 = in_18 ? register_3_q : 8'bz;  // Controlled_Buffer controlled_buffer_9
  and and_13 (and_13_out, decoder_1_out0, decoder_2_out1);
  and and_14 (and_14_out, decoder_1_out1, decoder_2_out1);
  and and_15 (and_15_out, decoder_1_out2, decoder_2_out1);
  and and_16 (and_16_out, decoder_1_out3, decoder_2_out1);
  and and_17 (and_17_out, and_13_out, Write_Enable);
  and and_18 (and_18_out, and_13_out, Read_Enable);
  and and_19 (and_19_out, and_14_out, Write_Enable);
  and and_20 (and_20_out, and_14_out, Read_Enable);
  and and_21 (and_21_out, and_15_out, Write_Enable);
  and and_22 (and_22_out, and_15_out, Read_Enable);
  and and_23 (and_23_out, and_16_out, Write_Enable);
  and and_24 (and_24_out, and_16_out, Read_Enable);
  assign D_in_out = and_18_out ? gated_latch_5_out_3 : 1'bz;  // Controlled_Buffer controlled_buffer_10
  Gated_Latch gated_latch_5 (.DATA(D_in_out), .WRITE_ENABLE_84b16714(and_17_out), .out_3(gated_latch_5_out_3));
  assign D_in_out = and_20_out ? gated_latch_6_out_3 : 1'bz;  // Controlled_Buffer controlled_buffer_11
  Gated_Latch gated_latch_6 (.DATA(D_in_out), .WRITE_ENABLE_84b16714(and_19_out), .out_3(gated_latch_6_out_3));
  assign D_in_out = and_22_out ? gated_latch_7_out_3 : 1'bz;  // Controlled_Buffer controlled_buffer_12
  Gated_Latch gated_latch_7 (.DATA(D_in_out), .WRITE_ENABLE_84b16714(and_21_out), .out_3(gated_latch_7_out_3));
  assign D_in_out = and_24_out ? gated_latch_8_out_3 : 1'bz;  // Controlled_Buffer controlled_buffer_13
  Gated_Latch gated_latch_8 (.DATA(D_in_out), .WRITE_ENABLE_84b16714(and_23_out), .out_3(gated_latch_8_out_3));
  assign out_28 = in_13 ? undriven : 8'bz;  // Controlled_Buffer controlled_buffer_14
  and and_25 (and_25_out, decoder_1_out0, decoder_2_out2);
  and and_26 (and_26_out, decoder_1_out1, decoder_2_out2);
  and and_27 (and_27_out, decoder_1_out2, decoder_2_out2);
  and and_28 (and_28_out, decoder_1_out3, decoder_2_out2);
  Memory_Chip memory_chip_1 ();  // open: REG_ADDR, OUT_ADDR_1, OUT_ADDR_2, DATA_IN, ENBL, CLR, CLK, in_8, OUT_DATA_1, OUT_DATA_2
  and and_29 (and_29_out, and_25_out, Write_Enable);
  and and_30 (and_30_out, and_25_out, Read_Enable);
  and and_31 (and_31_out, and_26_out, Write_Enable);
  and and_32 (and_32_out, and_26_out, Read_Enable);
  and and_33 (and_33_out, and_27_out, Write_Enable);
  and and_34 (and_34_out, and_27_out, Read_Enable);
  and and_35 (and_35_out, and_28_out, Write_Enable);
  and and_36 (and_36_out, and_28_out, Read_Enable);
  assign D_in_out = and_30_out ? gated_latch_9_out_3 : 1'bz;  // Controlled_Buffer controlled_buffer_15
  Gated_Latch gated_latch_9 (.DATA(D_in_out), .WRITE_ENABLE_84b16714(and_29_out), .out_3(gated_latch_9_out_3));
  assign D_in_out = and_32_out ? gated_latch_10_out_3 : 1'bz;  // Controlled_Buffer controlled_buffer_16
  Gated_Latch gated_latch_10 (.DATA(D_in_out), .WRITE_ENABLE_84b16714(and_31_out), .out_3(gated_latch_10_out_3));
  assign D_in_out = and_34_out ? gated_latch_11_out_3 : 1'bz;  // Controlled_Buffer controlled_buffer_17
  Gated_Latch gated_latch_11 (.DATA(D_in_out), .WRITE_ENABLE_84b16714(and_33_out), .out_3(gated_latch_11_out_3));
  assign D_in_out = and_36_out ? gated_latch_12_out_3 : 1'bz;  // Controlled_Buffer controlled_buffer_18
  Gated_Latch gated_latch_12 (.DATA(D_in_out), .WRITE_ENABLE_84b16714(and_35_out), .out_3(gated_latch_12_out_3));
  and and_37 (and_37_out, decoder_1_out0, decoder_2_out3);
  and and_38 (and_38_out, decoder_1_out1, decoder_2_out3);
  and and_39 (and_39_out, decoder_1_out2, decoder_2_out3);
  and and_40 (and_40_out, decoder_1_out3, decoder_2_out3);
  and and_41 (and_41_out, and_37_out, Write_Enable);
  and and_42 (and_42_out, and_37_out, Read_Enable);
  and and_43 (and_43_out, and_38_out, Write_Enable);
  and and_44 (and_44_out, and_38_out, Read_Enable);
  and and_45 (and_45_out, and_39_out, Write_Enable);
  and and_46 (and_46_out, and_39_out, Read_Enable);
  and and_47 (and_47_out, and_40_out, Write_Enable);
  and and_48 (and_48_out, and_40_out, Read_Enable);
  assign D_in_out = and_42_out ? gated_latch_13_out_3 : 1'bz;  // Controlled_Buffer controlled_buffer_19
  Gated_Latch gated_latch_13 (.DATA(D_in_out), .WRITE_ENABLE_84b16714(and_41_out), .out_3(gated_latch_13_out_3));
  assign D_in_out = and_44_out ? gated_latch_14_out_3 : 1'bz;  // Controlled_Buffer controlled_buffer_20
  Gated_Latch gated_latch_14 (.DATA(D_in_out), .WRITE_ENABLE_84b16714(and_43_out), .out_3(gated_latch_14_out_3));
  assign D_in_out = and_46_out ? gated_latch_15_out_3 : 1'bz;  // Controlled_Buffer controlled_buffer_21
  Gated_Latch gated_latch_15 (.DATA(D_in_out), .WRITE_ENABLE_84b16714(and_45_out), .out_3(gated_latch_15_out_3));
  assign D_in_out = and_48_out ? gated_latch_16_out_3 : 1'bz;  // Controlled_Buffer controlled_buffer_22
  Gated_Latch gated_latch_16 (.DATA(D_in_out), .WRITE_ENABLE_84b16714(and_47_out), .out_3(gated_latch_16_out_3));
endmodule

module Memory_Chip (
  input  [3:0] REG_ADDR,
  input  [3:0] OUT_ADDR_1,
  input  [3:0] OUT_ADDR_2,
  input  [7:0] DATA_IN,
  input  ENBL,
  input  CLR,
  input  CLK,
  input  in_8,
  output [7:0] OUT_DATA_1,
  output [7:0] OUT_DATA_2
);

  wire and_1_out, and_2_out, and_3_out, and_4_out, and_21_out, and_22_out, and_23_out, and_24_out,
       and_25_out, and_26_out, and_27_out, and_28_out, and_29_out, and_30_out, and_31_out, and_32_out;
  wire [3:0] and_5_out, and_9_out, and_13_out, decoder_1_out0, decoder_1_out4, decoder_1_out8,
       decoder_1_out12;
  wire [7:0] register_1_q, register_2_q, register_3_q, register_4_q, register_5_q, register_6_q,
       register_7_q, register_8_q, register_9_q, register_10_q, register_11_q, register_12_q, register_13_q,
       register_14_q, register_15_q, register_16_q;

  Decoder #(.enable("false"), .select(4)) decoder_1 (
    .out0(decoder_1_out0[0]), .out1(decoder_1_out0[1]), .out2(decoder_1_out0[2]), .out3(decoder_1_out0[3]),
    .out4(decoder_1_out4[0]), .out5(decoder_1_out4[1]), .out6(decoder_1_out4[2]), .out7(decoder_1_out4[3]),
    .out8(decoder_1_out8[0]), .out9(decoder_1_out8[1]), .out10(decoder_1_out8[2]), .out11(decoder_1_out8[3]),
    .out12(decoder_1_out12[0]), .out13(decoder_1_out12[1]), .out14(decoder_1_out12[2]),
    .out15(decoder_1_out12[3]), .sel(REG_ADDR));
  and and_1 (and_1_out, decoder_1_out0[0], ENBL);
  and and_2 (and_2_out, decoder_1_out0[1], ENBL);
  and and_3 (and_3_out, decoder_1_out0[2], ENBL);
  and and_4 (and_4_out, decoder_1_out0[3], ENBL);
  and and_5 (and_5_out[0], decoder_1_out4[0], ENBL);
  and and_6 (and_5_out[1], decoder_1_out4[1], ENBL);
  and and_7 (and_5_out[2], decoder_1_out4[2], ENBL);
  and and_8 (and_5_out[3], decoder_1_out4[3], ENBL);
  and and_9 (and_9_out[0], decoder_1_out8[0], ENBL);
  and and_10 (and_9_out[1], decoder_1_out8[1], ENBL);
  and and_11 (and_9_out[2], decoder_1_out8[2], ENBL);
  and and_12 (and_9_out[3], decoder_1_out8[3], ENBL);
  and and_13 (and_13_out[0], decoder_1_out12[0], ENBL);
  and and_14 (and_13_out[1], decoder_1_out12[1], ENBL);
  and and_15 (and_13_out[2], decoder_1_out12[2], ENBL);
  and and_16 (and_13_out[3], decoder_1_out12[3], ENBL);
  Register register_1 (.D(DATA_IN), .en(and_1_out), .clk(CLK), .Q(register_1_q), .clr(in_8));
  // AND_Gate and_17 has open pins: in0=and_1_out, in1=CLR, out=open
  Register register_2 (.D(DATA_IN), .en(and_2_out), .clk(CLK), .Q(register_2_q), .clr(in_8));
  and and_18 (in_8, and_2_out, CLR);
  Register register_3 (.D(DATA_IN), .en(and_3_out), .clk(CLK), .Q(register_3_q), .clr(in_8));
  and and_19 (in_8, and_3_out, CLR);
  Register register_4 (.D(DATA_IN), .en(and_4_out), .clk(CLK), .Q(register_4_q), .clr(in_8));
  and and_20 (in_8, and_4_out, CLR);
  Register register_5 (.D(DATA_IN), .en(and_5_out[0]), .clk(CLK), .Q(register_5_q), .clr(and_21_out));
  and and_21 (and_21_out, and_5_out[0], CLR);
  Register register_6 (.D(DATA_IN), .en(and_5_out[1]), .clk(CLK), .Q(register_6_q), .clr(and_22_out));
  and and_22 (and_22_out, and_5_out[1], CLR);
  Register register_7 (.D(DATA_IN), .en(and_5_out[2]), .clk(CLK), .Q(register_7_q), .clr(and_23_out));
  and and_23 (and_23_out, and_5_out[2], CLR);
  Register register_8 (.D(DATA_IN), .en(and_5_out[3]), .clk(CLK), .Q(register_8_q), .clr(and_24_out));
  and and_24 (and_24_out, and_5_out[3], CLR);
  Register register_9 (.D(DATA_IN), .en(and_9_out[0]), .clk(CLK), .Q(register_9_q), .clr(and_25_out));
  and and_25 (and_25_out, and_9_out[0], CLR);
  Register register_10 (.D(DATA_IN), .en(and_9_out[1]), .clk(CLK), .Q(register_10_q), .clr(and_26_out));
  and and_26 (and_26_out, and_9_out[1], CLR);
  Register register_11 (.D(DATA_IN), .en(and_9_out[2]), .clk(CLK), .Q(register_11_q), .clr(and_27_out));
  and and_27 (and_27_out, and_9_out[2], CLR);
  Register register_12 (.D(DATA_IN), .en(and_9_out[3]), .clk(CLK), .Q(register_12_q), .clr(and_28_out));
  and and_28 (and_28_out, and_9_out[3], CLR);
  Register register_13 (.D(DATA_IN), .en(and_13_out[0]), .clk(CLK), .Q(register_13_q), .clr(and_29_out));
  and and_29 (and_29_out, and_13_out[0], CLR);
  Register register_14 (.D(DATA_IN), .en(and_13_out[1]), .clk(CLK), .Q(register_14_q), .clr(and_30_out));
  and and_30 (and_30_out, and_13_out[1], CLR);
  Register register_15 (.D(DATA_IN), .en(and_13_out[2]), .clk(CLK), .Q(register_15_q), .clr(and_31_out));
  and and_31 (and_31_out, and_13_out[2], CLR);
  Register register_16 (.D(DATA_IN), .en(and_13_out[3]), .clk(CLK), .Q(register_16_q), .clr(and_32_out));
  and and_32 (and_32_out, and_13_out[3], CLR);
  Multiplexer #(.select(4), .width(8)) multiplexer_1 (
    .in0(register_1_q), .in1(register_2_q), .in2(register_3_q), .in3(register_4_q), .in4(register_5_q),
    .in5(register_6_q), .in6(register_7_q), .in7(register_8_q), .in8(register_9_q), .in9(register_10_q),
    .in10(register_11_q), .in11(register_12_q), .in12(register_13_q), .in13(register_14_q),
    .in14(register_15_q), .in15(register_16_q), .out(OUT_DATA_1), .sel(OUT_ADDR_1));
  Multiplexer #(.select(4), .width(8)) multiplexer_2 (
    .in0(register_1_q), .in1(register_2_q), .in2(register_3_q), .in3(register_4_q), .in4(register_5_q),
    .in5(register_6_q), .in6(register_7_q), .in7(register_8_q), .in8(register_9_q), .in9(register_10_q),
    .in10(register_11_q), .in11(register_12_q), .in12(register_13_q), .in13(register_14_q),
    .in14(register_15_q), .in15(register_16_q), .out(OUT_DATA_2), .sel(OUT_ADDR_2));
endmodule

module CU_Register (
  input  in_1,
  input  in_2,
  input  in_3,
  input  in_4,
  input  in_5,
  input  in_6,
  input  in_7,
  input  in_8
);

  wire controlled_buffer_1_out, register_1_q, register_2_q;

  Register #(.width(1)) register_1 (.D(controlled_buffer_1_out), .en(in_3), .clk(in_5), .Q(register_1_q), .clr(in_7));
  assign controlled_buffer_1_out = in_1 ? register_1_q : 1'bz;  // Controlled_Buffer controlled_buffer_1
  assign controlled_buffer_1_out = in_2 ? register_2_q : 1'bz;  // Controlled_Buffer controlled_buffer_2
  Register #(.width(1)) register_2 (.D(controlled_buffer_1_out), .en(in_4), .clk(in_6), .Q(register_2_q), .clr(in_8));
  // Probe on controlled_buffer_1_out
endmodule

module Control_Unit (
  input  [7:0] MAIN_BUS_IN,
  input  [7:0] ALU_OUTPUT,
  input  CLEAR,
  input  [7:0] INST_DATA,
  output [7:0] MAIN_BUS_OUT,
  output [7:0] A_INPUT,
  output [7:0] B_INPUT,
  output [1:0] OP_CODE,
  output [3:0] ADDRESS,
  output LOAD_READ_ENBL,
  output STORE_WRITE_ENBL,
  output [3:0] Counter_Address,
  output Counter_Load,
  output [3:0] Page_Select
);

  wire and_1_out, and_2_out, and_3_out, and_4_out, and_5_out, and_6_out, and_7_out, and_8_out, and_9_out,
       and_10_out, and_11_out, buffer_1_out, buffer_2_out, buffer_3_out, clock_1_out, clock_2_out,
       clock_3_out, decoder_2_out0, decoder_2_out1, decoder_2_out2, decoder_2_out3, decoder_3_out0,
       decoder_3_out3, decoder_4_out0, decoder_4_out1, decoder_4_out2, decoder_4_out3,
       n7_segment_display_1_p1, n7_segment_display_2_p1, n7_segment_display_3_p1, n7_segment_display_4_p1,
       n7_segment_display_5_p1, n7_segment_display_6_p1, n7_segment_display_7_p1, n7_segment_display_8_p1,
       n7_segment_display_9_p1, n7_segment_display_10_p1, n7_segment_display_11_p1, n7_segment_display_12_p1,
       not_1_out;
  wire [3:0] controlled_buffer_2_out, controlled_buffer_11_out, decoder_1_out0;
  wire [7:0] binary_to_bcd_converter_1_p1, binary_to_bcd_converter_2_p1, register_1_q, register_4_q,
       register_5_q;

  Multiplexer #(.select(2), .width(8)) multiplexer_1 (
    .in0(binary_to_bcd_converter_1_p1), .in1(binary_to_bcd_converter_2_p1), .in2(register_4_q),
    .in3(register_5_q), .out(A_INPUT), .sel(INST_DATA[3:2]));
  Multiplexer #(.select(2), .width(8)) multiplexer_2 (
    .in0(binary_to_bcd_converter_1_p1), .in1(binary_to_bcd_converter_2_p1), .in2(register_4_q),
    .in3(register_5_q), .out(B_INPUT), .sel(INST_DATA[1:0]));
  Decoder #(.enable("false"), .select(2)) decoder_1 (
    .out0(decoder_1_out0[0]), .out1(decoder_1_out0[1]), .out2(decoder_1_out0[2]), .out3(decoder_1_out0[3]),
    .sel(INST_DATA[3:2]));
  Register register_1 (.D(ALU_OUTPUT), .en(buffer_1_out), .clk(clock_1_out), .Q(register_1_q), .clr(CLEAR));
  Clock clock_1 (.out(clock_1_out));
  buf buffer_1 (buffer_1_out, decoder_3_out0);
  // BCD_to_7_Segment_decoder bcd_to_7_segment_decoder_1: pin names not known
  // BCD_to_7_Segment_decoder bcd_to_7_segment_decoder_2: pin names not known
  // _7_Segment_Display 7_segment_display_1: pin names not known; wires that end beside it: n7_segment_display_1_p1, n7_segment_display_1_p1
  // _7_Segment_Display 7_segment_display_2: pin names not known; wires that end beside it: n7_segment_display_2_p1, n7_segment_display_2_p1
  // Binary_to_BCD_converter #(.binvalue(8)) binary_to_bcd_converter_1: pin names not known; wires that end beside it: binary_to_bcd_converter_1_p1
  Clock clock_2 (.out(clock_2_out));
  assign MAIN_BUS_IN = and_1_out ? register_1_q : 8'bz;  // Controlled_Buffer controlled_buffer_1
  and and_1 (and_1_out, decoder_3_out0, clock_1_out);
  // BCD_to_7_Segment_decoder bcd_to_7_segment_decoder_3: pin names not known
  // _7_Segment_Display 7_segment_display_3: pin names not known; wires that end beside it: n7_segment_display_3_p1, n7_segment_display_3_p1
  Register register_2 (
    .D(MAIN_BUS_IN), .en(controlled_buffer_2_out[0]), .clk(buffer_3_out), .Q(binary_to_bcd_converter_1_p1),
    .clr(CLEAR));
  buf buffer_2 (buffer_2_out, clock_2_out);
  buf buffer_3 (buffer_3_out, buffer_2_out);
  assign controlled_buffer_2_out = and_1_out ? decoder_1_out0 : 4'bz;  // Controlled_Buffer controlled_buffer_2
  // BCD_to_7_Segment_decoder bcd_to_7_segment_decoder_4: pin names not known
  // _7_Segment_Display 7_segment_display_4: pin names not known; wires that end beside it: n7_segment_display_4_p1, n7_segment_display_4_p1
  // Binary_to_BCD_converter #(.binvalue(8)) binary_to_bcd_converter_2: pin names not known; wires that end beside it: binary_to_bcd_converter_2_p1
  assign MAIN_BUS_IN = and_2_out ? binary_to_bcd_converter_1_p1 : 8'bz;  // Controlled_Buffer controlled_buffer_3
  and and_2 (and_2_out, decoder_2_out0, STORE_WRITE_ENBL);
  // BCD_to_7_Segment_decoder bcd_to_7_segment_decoder_5: pin names not known
  // _7_Segment_Display 7_segment_display_5: pin names not known; wires that end beside it: n7_segment_display_5_p1, n7_segment_display_5_p1
  Register register_3 (
    .D(MAIN_BUS_IN), .en(controlled_buffer_2_out[1]), .clk(buffer_3_out), .Q(binary_to_bcd_converter_2_p1),
    .clr(CLEAR));
  not not_1 (not_1_out, and_1_out);
  and and_3 (and_3_out, decoder_2_out1, STORE_WRITE_ENBL);
  and and_4 (and_4_out, decoder_2_out2, STORE_WRITE_ENBL);
  and and_5 (and_5_out, decoder_2_out3, STORE_WRITE_ENBL);
  Decoder #(.enable("false"), .select(2)) decoder_2 (
    .out0(decoder_2_out0), .out1(decoder_2_out1), .out2(decoder_2_out2), .out3(decoder_2_out3),
    .sel(INST_DATA[5:4]));
  // BCD_to_7_Segment_decoder bcd_to_7_segment_decoder_6: pin names not known
  // _7_Segment_Display 7_segment_display_6: pin names not known; wires that end beside it: n7_segment_display_6_p1, n7_segment_display_6_p1
  assign MAIN_BUS_IN = and_3_out ? binary_to_bcd_converter_2_p1 : 8'bz;  // Controlled_Buffer controlled_buffer_4
  Register register_4 (
    .D(MAIN_BUS_IN), .en(controlled_buffer_2_out[2]), .clk(buffer_3_out), .Q(register_4_q), .clr(CLEAR));
  assign controlled_buffer_2_out[0] = not_1_out ? and_6_out : 1'bz;  // Controlled_Buffer controlled_buffer_5
  and and_6 (and_6_out, decoder_4_out0, LOAD_READ_ENBL);
  Decoder #(.enable("false"), .select(2)) decoder_3 (
    .out0(decoder_3_out0), .out1(LOAD_READ_ENBL), .out2(STORE_WRITE_ENBL), .out3(decoder_3_out3),
    .sel(INST_DATA[7:6]));
  // BCD_to_7_Segment_decoder bcd_to_7_segment_decoder_7: pin names not known
  // BCD_to_7_Segment_decoder bcd_to_7_segment_decoder_8: pin names not known
  // _7_Segment_Display 7_segment_display_7: pin names not known; wires that end beside it: n7_segment_display_7_p1, n7_segment_display_7_p1
  // _7_Segment_Display 7_segment_display_8: pin names not known; wires that end beside it: n7_segment_display_8_p1, n7_segment_display_8_p1
  // Binary_to_BCD_converter #(.binvalue(8)) binary_to_bcd_converter_3: pin names not known; wires that end beside it: register_4_q
  assign MAIN_BUS_IN = and_4_out ? register_4_q : 8'bz;  // Controlled_Buffer controlled_buffer_6
  assign controlled_buffer_2_out[1] = not_1_out ? and_7_out : 1'bz;  // Controlled_Buffer controlled_buffer_7
  assign controlled_buffer_2_out[2] = not_1_out ? and_8_out : 1'bz;  // Controlled_Buffer controlled_buffer_8
  assign controlled_buffer_2_out[3] = not_1_out ? and_9_out : 1'bz;  // Controlled_Buffer controlled_buffer_9
  and and_7 (and_7_out, decoder_4_out1, LOAD_READ_ENBL);
  and and_8 (and_8_out, decoder_4_out2, LOAD_READ_ENBL);
  and and_9 (and_9_out, decoder_4_out3, LOAD_READ_ENBL);
  Decoder #(.enable("false"), .select(2)) decoder_4 (
    .out0(decoder_4_out0), .out1(decoder_4_out1), .out2(decoder_4_out2), .out3(decoder_4_out3),
    .sel(INST_DATA[5:4]));
  // BCD_to_7_Segment_decoder bcd_to_7_segment_decoder_9: pin names not known
  // _7_Segment_Display 7_segment_display_9: pin names not known; wires that end beside it: n7_segment_display_9_p1, n7_segment_display_9_p1
  Register register_5 (
    .D(MAIN_BUS_IN), .en(controlled_buffer_2_out[3]), .clk(buffer_3_out), .Q(register_5_q), .clr(CLEAR));
  // BCD_to_7_Segment_decoder bcd_to_7_segment_decoder_10: pin names not known
  // _7_Segment_Display 7_segment_display_10: pin names not known; wires that end beside it: n7_segment_display_10_p1, n7_segment_display_10_p1
  // Binary_to_BCD_converter #(.binvalue(8)) binary_to_bcd_converter_4: pin names not known; wires that end beside it: register_5_q
  assign MAIN_BUS_IN = and_5_out ? register_5_q : 8'bz;  // Controlled_Buffer controlled_buffer_10
  // BCD_to_7_Segment_decoder bcd_to_7_segment_decoder_11: pin names not known
  // _7_Segment_Display 7_segment_display_11: pin names not known; wires that end beside it: n7_segment_display_11_p1, n7_segment_display_11_p1
  Clock clock_3 (.out(clock_3_out));
  and and_10 (and_10_out, INST_DATA[4], decoder_3_out3);
  assign controlled_buffer_11_out = and_11_out ? INST_DATA[3:0] : 4'bz;  // Controlled_Buffer controlled_buffer_11
  and and_11 (and_11_out, decoder_3_out3, INST_DATA[5]);
  // BCD_to_7_Segment_decoder bcd_to_7_segment_decoder_12: pin names not known
  // _7_Segment_Display 7_segment_display_12: pin names not known; wires that end beside it: n7_segment_display_12_p1, n7_segment_display_12_p1
  Register #(.width(4)) register_6 (
    .D(controlled_buffer_11_out), .en(and_11_out), .clk(clock_3_out), .Q(Page_Select), .clr(CLEAR));
  Register #(.width(4)) register_7 (
    .D(INST_DATA[3:0]), .en(and_10_out), .clk(clock_3_out), .Q(Counter_Address), .clr(CLEAR));
  D_Flip_Flop d_ff_1 (.D(and_10_out), .clk(clock_3_out), .Q(Counter_Load));  // open: Qn, preset, reset

  assign ADDRESS = INST_DATA[3:0];
  assign MAIN_BUS_OUT = MAIN_BUS_IN;
  assign OP_CODE = INST_DATA[5:4];
endmodule

module Paging_Registers (
  input  [3:0] PAGE_SELECT,
  input  [3:0] REG_ADDR,
  input  [7:0] DATA_IN,
  input  [3:0] OUT_ADDR_1,
  input  [3:0] OUT_ADDR_2,
  input  ENBL,
  input  CLK,
  output [7:0] OUT_DATA_1,
  output [7:0] OUT_DATA_2
);

  wire and_1_out, and_2_out, and_3_out, and_4_out;
  wire [3:0] and_5_out, and_9_out, and_13_out, decoder_1_out0, decoder_1_out4, decoder_1_out8,
       decoder_1_out12;
  wire [7:0] memory_chip_1_out_data_1, memory_chip_1_out_data_2, memory_chip_2_out_data_1,
       memory_chip_2_out_data_2, memory_chip_3_out_data_1, memory_chip_3_out_data_2,
       memory_chip_4_out_data_1, memory_chip_4_out_data_2, memory_chip_5_out_data_1,
       memory_chip_5_out_data_2, memory_chip_6_out_data_1, memory_chip_6_out_data_2,
       memory_chip_7_out_data_1, memory_chip_7_out_data_2, memory_chip_8_out_data_1,
       memory_chip_8_out_data_2, memory_chip_9_out_data_1, memory_chip_9_out_data_2,
       memory_chip_10_out_data_1, memory_chip_10_out_data_2, memory_chip_11_out_data_1,
       memory_chip_11_out_data_2, memory_chip_12_out_data_1, memory_chip_12_out_data_2,
       memory_chip_13_out_data_1, memory_chip_13_out_data_2, memory_chip_14_out_data_1,
       memory_chip_14_out_data_2, memory_chip_15_out_data_1, memory_chip_15_out_data_2,
       memory_chip_16_out_data_1, memory_chip_16_out_data_2;

  Decoder #(.enable("false"), .select(4)) decoder_1 (
    .out0(decoder_1_out0[0]), .out1(decoder_1_out0[1]), .out2(decoder_1_out0[2]), .out3(decoder_1_out0[3]),
    .out4(decoder_1_out4[0]), .out5(decoder_1_out4[1]), .out6(decoder_1_out4[2]), .out7(decoder_1_out4[3]),
    .out8(decoder_1_out8[0]), .out9(decoder_1_out8[1]), .out10(decoder_1_out8[2]), .out11(decoder_1_out8[3]),
    .out12(decoder_1_out12[0]), .out13(decoder_1_out12[1]), .out14(decoder_1_out12[2]),
    .out15(decoder_1_out12[3]), .sel(PAGE_SELECT));
  and and_1 (and_1_out, decoder_1_out0[0], ENBL);
  and and_2 (and_2_out, decoder_1_out0[1], ENBL);
  and and_3 (and_3_out, decoder_1_out0[2], ENBL);
  and and_4 (and_4_out, decoder_1_out0[3], ENBL);
  and and_5 (and_5_out[0], decoder_1_out4[0], ENBL);
  and and_6 (and_5_out[1], decoder_1_out4[1], ENBL);
  and and_7 (and_5_out[2], decoder_1_out4[2], ENBL);
  and and_8 (and_5_out[3], decoder_1_out4[3], ENBL);
  and and_9 (and_9_out[0], decoder_1_out8[0], ENBL);
  and and_10 (and_9_out[1], decoder_1_out8[1], ENBL);
  and and_11 (and_9_out[2], decoder_1_out8[2], ENBL);
  and and_12 (and_9_out[3], decoder_1_out8[3], ENBL);
  and and_13 (and_13_out[0], decoder_1_out12[0], ENBL);
  and and_14 (and_13_out[1], decoder_1_out12[1], ENBL);
  and and_15 (and_13_out[2], decoder_1_out12[2], ENBL);
  and and_16 (and_13_out[3], decoder_1_out12[3], ENBL);
  assign OUT_DATA_1 = decoder_1_out0[0] ? memory_chip_1_out_data_1 : 8'bz;  // Controlled_Buffer controlled_buffer_1
  assign OUT_DATA_2 = decoder_1_out0[0] ? memory_chip_1_out_data_2 : 8'bz;  // Controlled_Buffer controlled_buffer_2
  assign OUT_DATA_1 = decoder_1_out0[1] ? memory_chip_2_out_data_1 : 8'bz;  // Controlled_Buffer controlled_buffer_3
  assign OUT_DATA_2 = decoder_1_out0[1] ? memory_chip_2_out_data_2 : 8'bz;  // Controlled_Buffer controlled_buffer_4
  assign OUT_DATA_1 = decoder_1_out0[2] ? memory_chip_3_out_data_1 : 8'bz;  // Controlled_Buffer controlled_buffer_5
  assign OUT_DATA_2 = decoder_1_out0[2] ? memory_chip_3_out_data_2 : 8'bz;  // Controlled_Buffer controlled_buffer_6
  assign OUT_DATA_1 = decoder_1_out0[3] ? memory_chip_4_out_data_1 : 8'bz;  // Controlled_Buffer controlled_buffer_7
  assign OUT_DATA_2 = decoder_1_out0[3] ? memory_chip_4_out_data_2 : 8'bz;  // Controlled_Buffer controlled_buffer_8
  Memory_Chip memory_chip_1 (
    .REG_ADDR(REG_ADDR), .OUT_ADDR_1(OUT_ADDR_1), .OUT_ADDR_2(OUT_ADDR_2), .DATA_IN(DATA_IN),
    .ENBL(and_1_out), .CLK(CLK), .OUT_DATA_1(memory_chip_1_out_data_1), .OUT_DATA_2(memory_chip_1_out_data_2));  // open: CLR, in_8
  Memory_Chip memory_chip_2 (
    .REG_ADDR(REG_ADDR), .OUT_ADDR_1(OUT_ADDR_1), .OUT_ADDR_2(OUT_ADDR_2), .DATA_IN(DATA_IN),
    .ENBL(and_2_out), .CLK(CLK), .OUT_DATA_1(memory_chip_2_out_data_1), .OUT_DATA_2(memory_chip_2_out_data_2));  // open: CLR, in_8
  Memory_Chip memory_chip_3 (
    .REG_ADDR(REG_ADDR), .OUT_ADDR_1(OUT_ADDR_1), .OUT_ADDR_2(OUT_ADDR_2), .DATA_IN(DATA_IN),
    .ENBL(and_3_out), .CLK(CLK), .OUT_DATA_1(memory_chip_3_out_data_1), .OUT_DATA_2(memory_chip_3_out_data_2));  // open: CLR, in_8
  Memory_Chip memory_chip_4 (
    .REG_ADDR(REG_ADDR), .OUT_ADDR_1(OUT_ADDR_1), .OUT_ADDR_2(OUT_ADDR_2), .DATA_IN(DATA_IN),
    .ENBL(and_4_out), .CLK(CLK), .OUT_DATA_1(memory_chip_4_out_data_1), .OUT_DATA_2(memory_chip_4_out_data_2));  // open: CLR, in_8
  assign OUT_DATA_1 = decoder_1_out4[0] ? memory_chip_5_out_data_1 : 8'bz;  // Controlled_Buffer controlled_buffer_9
  assign OUT_DATA_2 = decoder_1_out4[0] ? memory_chip_5_out_data_2 : 8'bz;  // Controlled_Buffer controlled_buffer_10
  assign OUT_DATA_1 = decoder_1_out4[1] ? memory_chip_6_out_data_1 : 8'bz;  // Controlled_Buffer controlled_buffer_11
  assign OUT_DATA_2 = decoder_1_out4[1] ? memory_chip_6_out_data_2 : 8'bz;  // Controlled_Buffer controlled_buffer_12
  assign OUT_DATA_1 = decoder_1_out4[2] ? memory_chip_7_out_data_1 : 8'bz;  // Controlled_Buffer controlled_buffer_13
  assign OUT_DATA_2 = decoder_1_out4[2] ? memory_chip_7_out_data_2 : 8'bz;  // Controlled_Buffer controlled_buffer_14
  assign OUT_DATA_1 = decoder_1_out4[3] ? memory_chip_8_out_data_1 : 8'bz;  // Controlled_Buffer controlled_buffer_15
  assign OUT_DATA_2 = decoder_1_out4[3] ? memory_chip_8_out_data_2 : 8'bz;  // Controlled_Buffer controlled_buffer_16
  Memory_Chip memory_chip_5 (
    .REG_ADDR(REG_ADDR), .OUT_ADDR_1(OUT_ADDR_1), .OUT_ADDR_2(OUT_ADDR_2), .DATA_IN(DATA_IN),
    .ENBL(and_5_out[0]), .CLK(CLK), .OUT_DATA_1(memory_chip_5_out_data_1),
    .OUT_DATA_2(memory_chip_5_out_data_2));  // open: CLR, in_8
  Memory_Chip memory_chip_6 (
    .REG_ADDR(REG_ADDR), .OUT_ADDR_1(OUT_ADDR_1), .OUT_ADDR_2(OUT_ADDR_2), .DATA_IN(DATA_IN),
    .ENBL(and_5_out[1]), .CLK(CLK), .OUT_DATA_1(memory_chip_6_out_data_1),
    .OUT_DATA_2(memory_chip_6_out_data_2));  // open: CLR, in_8
  Memory_Chip memory_chip_7 (
    .REG_ADDR(REG_ADDR), .OUT_ADDR_1(OUT_ADDR_1), .OUT_ADDR_2(OUT_ADDR_2), .DATA_IN(DATA_IN),
    .ENBL(and_5_out[2]), .CLK(CLK), .OUT_DATA_1(memory_chip_7_out_data_1),
    .OUT_DATA_2(memory_chip_7_out_data_2));  // open: CLR, in_8
  Memory_Chip memory_chip_8 (
    .REG_ADDR(REG_ADDR), .OUT_ADDR_1(OUT_ADDR_1), .OUT_ADDR_2(OUT_ADDR_2), .DATA_IN(DATA_IN),
    .ENBL(and_5_out[3]), .CLK(CLK), .OUT_DATA_1(memory_chip_8_out_data_1),
    .OUT_DATA_2(memory_chip_8_out_data_2));  // open: CLR, in_8
  assign OUT_DATA_1 = decoder_1_out8[0] ? memory_chip_9_out_data_1 : 8'bz;  // Controlled_Buffer controlled_buffer_17
  assign OUT_DATA_2 = decoder_1_out8[0] ? memory_chip_9_out_data_2 : 8'bz;  // Controlled_Buffer controlled_buffer_18
  assign OUT_DATA_1 = decoder_1_out8[1] ? memory_chip_10_out_data_1 : 8'bz;  // Controlled_Buffer controlled_buffer_19
  assign OUT_DATA_2 = decoder_1_out8[1] ? memory_chip_10_out_data_2 : 8'bz;  // Controlled_Buffer controlled_buffer_20
  assign OUT_DATA_1 = decoder_1_out8[2] ? memory_chip_11_out_data_1 : 8'bz;  // Controlled_Buffer controlled_buffer_21
  assign OUT_DATA_2 = decoder_1_out8[2] ? memory_chip_11_out_data_2 : 8'bz;  // Controlled_Buffer controlled_buffer_22
  assign OUT_DATA_1 = decoder_1_out8[3] ? memory_chip_12_out_data_1 : 8'bz;  // Controlled_Buffer controlled_buffer_23
  assign OUT_DATA_2 = decoder_1_out8[3] ? memory_chip_12_out_data_2 : 8'bz;  // Controlled_Buffer controlled_buffer_24
  Memory_Chip memory_chip_9 (
    .REG_ADDR(REG_ADDR), .OUT_ADDR_1(OUT_ADDR_1), .OUT_ADDR_2(OUT_ADDR_2), .DATA_IN(DATA_IN),
    .ENBL(and_9_out[0]), .CLK(CLK), .OUT_DATA_1(memory_chip_9_out_data_1),
    .OUT_DATA_2(memory_chip_9_out_data_2));  // open: CLR, in_8
  Memory_Chip memory_chip_10 (
    .REG_ADDR(REG_ADDR), .OUT_ADDR_1(OUT_ADDR_1), .OUT_ADDR_2(OUT_ADDR_2), .DATA_IN(DATA_IN),
    .ENBL(and_9_out[1]), .CLK(CLK), .OUT_DATA_1(memory_chip_10_out_data_1),
    .OUT_DATA_2(memory_chip_10_out_data_2));  // open: CLR, in_8
  Memory_Chip memory_chip_11 (
    .REG_ADDR(REG_ADDR), .OUT_ADDR_1(OUT_ADDR_1), .OUT_ADDR_2(OUT_ADDR_2), .DATA_IN(DATA_IN),
    .ENBL(and_9_out[2]), .CLK(CLK), .OUT_DATA_1(memory_chip_11_out_data_1),
    .OUT_DATA_2(memory_chip_11_out_data_2));  // open: CLR, in_8
  Memory_Chip memory_chip_12 (
    .REG_ADDR(REG_ADDR), .OUT_ADDR_1(OUT_ADDR_1), .OUT_ADDR_2(OUT_ADDR_2), .DATA_IN(DATA_IN),
    .ENBL(and_9_out[3]), .CLK(CLK), .OUT_DATA_1(memory_chip_12_out_data_1),
    .OUT_DATA_2(memory_chip_12_out_data_2));  // open: CLR, in_8
  assign OUT_DATA_1 = decoder_1_out12[0] ? memory_chip_13_out_data_1 : 8'bz;  // Controlled_Buffer controlled_buffer_25
  assign OUT_DATA_2 = decoder_1_out12[0] ? memory_chip_13_out_data_2 : 8'bz;  // Controlled_Buffer controlled_buffer_26
  assign OUT_DATA_1 = decoder_1_out12[1] ? memory_chip_14_out_data_1 : 8'bz;  // Controlled_Buffer controlled_buffer_27
  assign OUT_DATA_2 = decoder_1_out12[1] ? memory_chip_14_out_data_2 : 8'bz;  // Controlled_Buffer controlled_buffer_28
  assign OUT_DATA_1 = decoder_1_out12[2] ? memory_chip_15_out_data_1 : 8'bz;  // Controlled_Buffer controlled_buffer_29
  assign OUT_DATA_2 = decoder_1_out12[2] ? memory_chip_15_out_data_2 : 8'bz;  // Controlled_Buffer controlled_buffer_30
  assign OUT_DATA_1 = decoder_1_out12[3] ? memory_chip_16_out_data_1 : 8'bz;  // Controlled_Buffer controlled_buffer_31
  assign OUT_DATA_2 = decoder_1_out12[3] ? memory_chip_16_out_data_2 : 8'bz;  // Controlled_Buffer controlled_buffer_32
  Memory_Chip memory_chip_13 (
    .REG_ADDR(REG_ADDR), .OUT_ADDR_1(OUT_ADDR_1), .OUT_ADDR_2(OUT_ADDR_2), .DATA_IN(DATA_IN),
    .ENBL(and_13_out[0]), .CLK(CLK), .OUT_DATA_1(memory_chip_13_out_data_1),
    .OUT_DATA_2(memory_chip_13_out_data_2));  // open: CLR, in_8
  Memory_Chip memory_chip_14 (
    .REG_ADDR(REG_ADDR), .OUT_ADDR_1(OUT_ADDR_1), .OUT_ADDR_2(OUT_ADDR_2), .DATA_IN(DATA_IN),
    .ENBL(and_13_out[1]), .CLK(CLK), .OUT_DATA_1(memory_chip_14_out_data_1),
    .OUT_DATA_2(memory_chip_14_out_data_2));  // open: CLR, in_8
  Memory_Chip memory_chip_15 (
    .REG_ADDR(REG_ADDR), .OUT_ADDR_1(OUT_ADDR_1), .OUT_ADDR_2(OUT_ADDR_2), .DATA_IN(DATA_IN),
    .ENBL(and_13_out[2]), .CLK(CLK), .OUT_DATA_1(memory_chip_15_out_data_1),
    .OUT_DATA_2(memory_chip_15_out_data_2));  // open: CLR, in_8
  Memory_Chip memory_chip_16 (
    .REG_ADDR(REG_ADDR), .OUT_ADDR_1(OUT_ADDR_1), .OUT_ADDR_2(OUT_ADDR_2), .DATA_IN(DATA_IN),
    .ENBL(and_13_out[3]), .CLK(CLK), .OUT_DATA_1(memory_chip_16_out_data_1),
    .OUT_DATA_2(memory_chip_16_out_data_2));  // open: CLR, in_8
endmodule
